# Fritzing sketch LED Strip lighting controller (saved by Fritzing 0.9.3b)
breadboards: 1

parts:
  Part1 = Arduino Pro Mini v13
  CAPSENSE1 = AT42QT1010 Momentary Capsense Breakout
  CAPSENSE2 = AT42QT1010 Momentary Capsense Breakout
  Part2 = VERTER 5V USB Buck-Boost
  BAT1 = BC9VPC [package=bc9vpc]
  U1 = LIPO-2000mAh [package=lipo-2000]
  LDR = Photocell (LDR) [package=THT]
  Q1 = MOSFET-NCHANNEL [package=to220v]
  Q2 = MOSFET-NCHANNEL [package=to220v]
  LED_Strip_2 = LED - 3mm [color="White (6500K)" package="3 mm [THT]"]
  LED_Strip_1 = LED - 3mm [color="White (6500K)" package="3 mm [THT]"]
  R2 = Resistor [tolerance=±5% resistance=10k package=THT]
  R3 = Resistor [tolerance=±5% resistance=10k package=THT]
  R4 = Resistor [tolerance=±5% resistance=10k package=THT]
  R5 = Resistor [tolerance=±5% resistance=10k package=THT]
  R6 = Resistor [tolerance=±5% resistance=10k package=THT]

nets:
  VDD: Part1.VCC, CAPSENSE1.VDD, CAPSENSE2.VDD, Part2.5.0V, LDR.pin_0, R5.Pin_0, R6.Pin_0
  GND: Part1.GND, CAPSENSE1.GND, CAPSENSE2.GND, Part2.GND, U1.-, Q1.S, Q2.S, R2.Pin_1, R3.Pin_0, R4.Pin_0
  N1: Part1.A0, LDR.pin_1, R2.Pin_0
  N2: Part1.D6_PWM, Q1.G, R3.Pin_1
  N3: Part1.D5_PWM, Q2.G, R4.Pin_1
  N4: Part1.D3_PWM, CAPSENSE1.OUT, R6.Pin_1
  N5: Part1.D2, CAPSENSE2.OUT, R5.Pin_1
  N6: Part2.VIN, BAT1.V+, LED_Strip_2.anode, LED_Strip_1.anode
  N7: BAT1.V-, U1.+
  N8: Q1.D, LED_Strip_1.cathode
  N9: Q2.D, LED_Strip_2.cathode

custom parts:
  AT42QT1010 Momentary Capsense Breakout: A capacitive touch momentary switch breakout for the AT42QT1010 chip.
  VERTER 5V USB Buck-Boost: VERTER can take battery voltages from 3-12VDC and output a nice 5V DC, which makes it a perfect universal power supply for your portable project! Where Verter really shines is when you have a battery or power range that can fluctuate a lot, or you don't know what you'll end up using.
